# Fritzing sketch remote_breadbord (saved by Fritzing 0.9.3b)
circuit board: 8cm x 16cm
breadboards: 3

parts:
  S20 = Pushbutton [package="[THT]"]
  S21 = Pushbutton [package="[THT]"]
  S23 = Pushbutton [package="[THT]"]
  S22 = Pushbutton [package="[THT]"]
  S12 = Pushbutton [package="[THT]"]
  S14 = Pushbutton [package="[THT]"]
  S13 = Pushbutton [package="[THT]"]
  S15 = Pushbutton [package="[THT]"]
  S3 = Pushbutton [package="[THT]"]
  S2 = Pushbutton [package="[THT]"]
  S8 = Pushbutton [package="[THT]"]
  S16 = Pushbutton [package="[THT]"]
  S10 = Pushbutton [package="[THT]"]
  S11 = Pushbutton [package="[THT]"]
  S1 = Pushbutton [package="[THT]"]
  S9 = Pushbutton [package="[THT]"]
  S0 = Pushbutton [package="[THT]"]
  S17 = Pushbutton [package="[THT]"]
  S18 = Pushbutton [package="[THT]"]
  S19 = Pushbutton [package="[THT]"]
  S7 = Pushbutton [package="[THT]"]
  S6 = Pushbutton [package="[THT]"]
  S5 = Pushbutton [package="[THT]"]
  S4 = Pushbutton [package="[THT]"]
  U4 = 74HC165 [part_number=SN74LS165 package="DIP16 [THT]"]
  U5 = 74HC165 [part_number=SN74LS165 package="DIP16 [THT]"]
  U6 = 74HC165 [part_number=SN74LS165 package="DIP16 [THT]"]
  IC1 = 74HC4078 [package="DIP 14 (Dual Inline) [THT]"]
  IC2 = 74HC4078 [package="DIP 14 (Dual Inline) [THT]"]
  IC3 = 74HC4078 [package="DIP 14 (Dual Inline) [THT]"]
  R7 = Resistor [tolerance=±5% resistance=10k package=THT]
  R0 = Resistor [tolerance=±5% resistance=10k package=THT]
  R1 = Resistor [tolerance=±5% resistance=10k package=THT]
  R2 = Resistor [tolerance=±5% resistance=10k package=THT]
  R3 = Resistor [tolerance=±5% resistance=10k package=THT]
  R8 = Resistor [tolerance=±5% resistance=10k package=THT]
  R9 = Resistor [tolerance=±5% resistance=10k package=THT]
  R10 = Resistor [tolerance=±5% resistance=10k package=THT]
  R11 = Resistor [tolerance=±5% resistance=10k package=THT]
  R16 = Resistor [tolerance=±5% resistance=10k package=THT]
  R17 = Resistor [tolerance=±5% resistance=10k package=THT]
  R18 = Resistor [tolerance=±5% resistance=10k package=THT]
  R19 = Resistor [tolerance=±5% resistance=10k package=THT]
  R6 = Resistor [tolerance=±5% resistance=10k package=THT]
  R5 = Resistor [tolerance=±5% resistance=10k package=THT]
  R4 = Resistor [tolerance=±5% resistance=10k package=THT]
  R15 = Resistor [tolerance=±5% resistance=10k package=THT]
  R14 = Resistor [tolerance=±5% resistance=10k package=THT]
  R13 = Resistor [tolerance=±5% resistance=10k package=THT]
  R12 = Resistor [tolerance=±5% resistance=10k package=THT]
  R23 = Resistor [tolerance=±5% resistance=10k package=THT]
  R22 = Resistor [tolerance=±5% resistance=10k package=THT]
  R21 = Resistor [tolerance=±5% resistance=10k package=THT]
  R20 = Resistor [tolerance=±5% resistance=10k package=THT]
  LED1 = LED - 5mm [color="Infrared (940nm)" package="5 mm [THT]"]
  74HC1 = 74HC4075 [package="DIP 14 (Dual Inline) [THT]"]
  Q1 = NPN-Transistor [package="TO92 [THT]"]
  R25 = Resistor [tolerance=±5% resistance=470 package=THT]
  R26 = Resistor [tolerance=±5% resistance=100 package=THT]
  VCC1 = Battery
  ATtiny85 = ATTINY85 [package=dip]  # not connected
  ATtiny85_2 = ATTINY85 [package=dip]  # not connected

nets:
  VCC: S20.Pin_1, S20.Pin_2, S20.Pin_3, S20.Pin_4, S21.Pin_1, S21.Pin_2, S21.Pin_3, S21.Pin_4, S23.Pin_1, S23.Pin_2, S23.Pin_3, S23.Pin_4, S22.Pin_1, S22.Pin_2, S22.Pin_3, S22.Pin_4, S12.Pin_1, S12.Pin_2, S12.Pin_3, S12.Pin_4, S14.Pin_1, S14.Pin_2, S14.Pin_3, S14.Pin_4, S13.Pin_1, S13.Pin_2, S13.Pin_3, S13.Pin_4, S15.Pin_1, S15.Pin_2, S15.Pin_3, S15.Pin_4, S7.Pin_1, S7.Pin_2, S7.Pin_3, S7.Pin_4, S6.Pin_1, S6.Pin_2, S6.Pin_3, S6.Pin_4, S5.Pin_1, S5.Pin_2, S5.Pin_3, S5.Pin_4, S4.Pin_1, S4.Pin_2, S4.Pin_3, S4.Pin_4, U4.SH_CP, U4.ST_CP, U4.OE, U4.DS, U4.VCC, U5.SH_CP, U5.ST_CP, U5.OE, U5.DS, U5.VCC, U6.SH_CP, U6.ST_CP, U6.OE, U6.DS, U6.VCC, IC1.pin9, IC1.pin10, IC1.pin11, IC1.pin12, IC1.pin14, IC2.pin9, IC2.pin10, IC2.pin11, IC2.pin12, IC2.pin14, IC3.pin9, IC3.pin10, IC3.pin11, IC3.pin12, IC3.pin14, R7.Pin_0, R6.Pin_0, R5.Pin_0, R4.Pin_0, R15.Pin_0, R14.Pin_0, R13.Pin_0, R12.Pin_0, R23.Pin_0, R22.Pin_0, R21.Pin_0, R20.Pin_0, 74HC1.pin14, R26.Pin_0
  N1: S3.Pin_1, S3.Pin_2, S2.Pin_1, S2.Pin_2, S8.Pin_3, S8.Pin_4, S16.Pin_1, S16.Pin_2, S10.Pin_3, S10.Pin_4, S11.Pin_1, S11.Pin_2, S1.Pin_1, S1.Pin_2, S9.Pin_3, S9.Pin_4, S0.Pin_1, S0.Pin_2, S17.Pin_1, S17.Pin_2, S18.Pin_1, S18.Pin_2, S19.Pin_3, S19.Pin_4, VCC1.+
  N2: S3.Pin_3, S3.Pin_4, S2.Pin_3, S2.Pin_4, S8.Pin_1, S8.Pin_2, S16.Pin_3, S16.Pin_4, S10.Pin_1, S10.Pin_2, S11.Pin_3, S11.Pin_4, S1.Pin_3, S1.Pin_4, S9.Pin_1, S9.Pin_2, S0.Pin_3, S0.Pin_4, S19.Pin_1, S19.Pin_2, U4.Q3, U4.Q4, U4.Q5, U4.Q6, U5.Q3, U5.Q4, U5.Q5, U5.Q6, U6.Q3, U6.Q6, IC1.pin2, IC1.pin5, IC2.pin2, IC2.pin3, IC2.pin4, IC2.pin5, IC3.pin2, IC3.pin3, IC3.pin4, IC3.pin5, R0.Pin_1, R1.Pin_1, R2.Pin_1, R3.Pin_1, R8.Pin_1, R9.Pin_1, R10.Pin_1, R11.Pin_1, R16.Pin_1, R19.Pin_1
  N3: S17.Pin_3, S17.Pin_4, U6.Q5, IC1.pin4, R17.Pin_1
  N4: S18.Pin_3, S18.Pin_4, U6.Q4, IC1.pin3, R18.Pin_1
  N5: U4.Q1, U5.Q1, U6.Q1
  N6: U4.Q2, U5.Q2, U6.Q2
  GND: U4.GND, U4.Q0, U5.GND, U5.Q0, U6.GND, U6.Q0, IC1.pin7, IC2.pin7, IC3.pin7, R7.Pin_1, R0.Pin_0, R1.Pin_0, R2.Pin_0, R3.Pin_0, R8.Pin_0, R9.Pin_0, R10.Pin_0, R11.Pin_0, R16.Pin_0, R17.Pin_0, R19.Pin_0, R6.Pin_1, R5.Pin_1, R4.Pin_1, R15.Pin_1, R14.Pin_1, R13.Pin_1, R12.Pin_1, R23.Pin_1, R22.Pin_1, R21.Pin_1, R20.Pin_1, 74HC1.pin7, Q1.C, VCC1.-
  N7: U4.MR, U5.Q7'
  N8: U5.MR, U6.Q7'
  N9: IC1.pin1, 74HC1.pin5
  N10: IC2.pin1, 74HC1.pin4
  N11: IC3.pin1, 74HC1.pin3
  N12: LED1.cathode, R26.Pin_1
  N13: LED1.anode, Q1.E
  N14: Q1.B, R25.Pin_0

custom parts:
  74HC165: 8-bit parallel-load shift registers
  74HC4078: 8-input NOR/OR gate
  74HC4075: Triple 3-input OR gate
  ATTINY85: Atmel 8-pin 2/4/8kB flash uC
